# Fritzing sketch practica1 (saved by Fritzing 0.9.2b)
breadboards: 1

parts:
  Parte1 = Arduino Uno (Rev3)
  LED1 = LED - 5mm [color="Orange (620nm)" package="5 mm [THT]"]

nets:
  N1: Parte1.5V, LED1.anode
  N2: Parte1.GND, LED1.cathode
